// Logisim project alu.circ as structural Verilog: 1 circuit, main circuit alu
module alu (
  input  [31:0] A,
  input  [31:0] B,
  input  [3:0] ALUSel,
  output [31:0] ALUResult
);

  wire comparator_1_eq, comparator_1_gt, comparator_1_lt, comparator_2_eq, comparator_2_gt, comparator_2_lt,
       comparator_3_eq, comparator_3_gt, comparator_3_lt, comparator_4_lt, or_1_out, or_2_out, or_3_out;
  wire [4:0] and_1_out, and_2_out, and_3_out, bit_extender_1_out, bit_extender_2_out, bit_extender_3_out,
       bit_extender_4_out, bit_extender_5_out, bit_extender_10_out, bit_extender_12_out, bit_extender_13_out,
       bit_extender_14_out, or_4_out, or_5_out, or_7_out;
  wire [31:0] add0, and7, bit_extender_11_out, bit_extender_15_out, bit_extender_17_out, mul8, mulh9,
       mulhu11, multiplexer_2_out, multiplexer_3_out, multiplier_4_out, or6, shifter_1_out, shifter_2_out,
       shifter_8_out, sll1, slt2, sra13, srl5, sub12, undriven, undriven_2, undriven_3, xor4;
  wire [63:0] bit_extender_6_out, bit_extender_7_out, bit_extender_8_out, bit_extender_9_out,
       multiplier_2_out, multiplier_3_out, shifter_5_out, shifter_6_out;

  Multiplexer #(.enable("false"), .select(4), .width(32)) multiplexer_1 (
    .in0(add0), .in1(sll1), .in2(slt2), .in3(undriven), .in4(xor4), .in5(srl5), .in6(or6), .in7(and7),
    .in8(mul8), .in9(mulh9), .in10(undriven_2), .in11(mulhu11), .in12(sub12), .in13(sra13),
    .in14(undriven_3), .in15(B), .out(ALUResult), .sel(ALUSel));
  Comparator #(.mode("unsigned"), .width(32)) comparator_1 (
    .a(32'h1e), .b(32'h20), .gt(comparator_1_gt), .eq(comparator_1_eq), .lt(comparator_1_lt));
  Comparator #(.mode("unsigned"), .width(32)) comparator_2 (
    .a(32'h64), .b(32'h20), .gt(comparator_2_gt), .eq(comparator_2_eq), .lt(comparator_2_lt));
  // Probe on or_1_out
  or or_1 (or_1_out, comparator_2_gt, comparator_2_eq);
  assign bit_extender_1_out = {{4{comparator_2_lt}}, comparator_2_lt};  // Bit_Extender bit_extender_1
  Comparator #(.mode("unsigned"), .width(32)) comparator_3 (
    .a(B), .b(32'h20), .gt(comparator_3_gt), .eq(comparator_3_eq), .lt(comparator_3_lt));
  // Probe on or_2_out
  or or_2 (or_2_out, comparator_1_gt, comparator_1_eq);
  assign bit_extender_2_out = {{4{comparator_1_lt}}, comparator_1_lt};  // Bit_Extender bit_extender_2
  or or_3 (or_3_out, comparator_3_gt, comparator_3_eq);
  assign bit_extender_3_out = {{4{comparator_3_lt}}, comparator_3_lt};  // Bit_Extender bit_extender_3
  assign bit_extender_4_out = {{4{or_2_out}}, or_2_out};  // Bit_Extender bit_extender_4
  // Probe on and_1_out
  assign and_1_out = bit_extender_2_out & 5'b11110;  // AND_Gate and_1, 5 bits wide
  assign bit_extender_5_out = {{4{or_1_out}}, or_1_out};  // Bit_Extender bit_extender_5
  // Probe on and_2_out
  assign and_2_out = bit_extender_1_out & 5'b11110;  // AND_Gate and_2, 5 bits wide
  assign bit_extender_6_out = {{32{A[31]}}, A};  // Bit_Extender bit_extender_6
  assign bit_extender_7_out = {{32{B[31]}}, B};  // Bit_Extender bit_extender_7
  assign bit_extender_8_out = {{32{1'b0}}, A};  // Bit_Extender bit_extender_8
  assign bit_extender_9_out = {{32{1'b0}}, B};  // Bit_Extender bit_extender_9
  assign bit_extender_10_out = {{4{or_3_out}}, or_3_out};  // Bit_Extender bit_extender_10
  assign and_3_out = bit_extender_3_out & B[4:0];  // AND_Gate and_3, 5 bits wide
  assign or_4_out = bit_extender_4_out | and_1_out;  // OR_Gate or_4, 5 bits wide
  assign bit_extender_11_out = {{31{1'b1}}, 1'b1};  // Bit_Extender bit_extender_11
  assign or_5_out = bit_extender_5_out | and_2_out;  // OR_Gate or_5, 5 bits wide
  Adder #(.width(32)) adder_1 (.a(A), .b(B), .out(add0));  // open: cin, cout
  Bit_Extender #(.in_width(32), .out_width(5)) bit_extender_12 (.in(B), .out(bit_extender_12_out));
  Comparator #(.width(32)) comparator_4 (.a(A), .b(B), .lt(comparator_4_lt));  // open: gt, eq
  assign xor4 = A ^ B;  // XOR_Gate xor_1, 32 bits wide
  Bit_Extender #(.in_width(32), .out_width(5)) bit_extender_13 (.in(B), .out(bit_extender_13_out));
  assign or6 = A | B;  // OR_Gate or_6, 32 bits wide
  assign and7 = A & B;  // AND_Gate and_4, 32 bits wide
  Multiplier #(.mode("twosComplement"), .width(32)) multiplier_1 (.a(A), .b(B), .out(mul8));  // open: cin, cout
  Multiplier #(.mode("twosComplement"), .width(64)) multiplier_2 (
    .a(bit_extender_6_out), .b(bit_extender_7_out), .out(multiplier_2_out));  // open: cin, cout
  Multiplier #(.width(64)) multiplier_3 (
    .a(bit_extender_8_out), .b(bit_extender_9_out), .out(multiplier_3_out));  // open: cin, cout
  Adder #(.width(32)) adder_2 (.a(A), .b(multiplier_4_out), .out(sub12));  // open: cin, cout
  Multiplier #(.width(32)) multiplier_4 (.a({32{1'b1}}), .b(B), .out(multiplier_4_out));  // open: cin, cout
  Bit_Extender #(.in_width(32), .out_width(5)) bit_extender_14 (.in(B), .out(bit_extender_14_out));
  assign or_7_out = bit_extender_10_out | and_3_out;  // OR_Gate or_7, 5 bits wide
  Multiplexer #(.enable("false"), .width(32)) multiplexer_2 (
    .in0(bit_extender_15_out), .in1(shifter_1_out), .out(multiplexer_2_out), .sel(or_2_out));
  assign bit_extender_15_out = {{31{1'b1}}, 1'b1};  // Bit_Extender bit_extender_15
  Shifter #(.shift("ar"), .width(32)) shifter_1 (.in(32'habcde000), .\dist (or_4_out), .out(shifter_1_out));
  // Probe on shifter_1_out
  // Probe on multiplexer_3_out
  Multiplexer #(.enable("false"), .width(32)) multiplexer_3 (
    .in0(bit_extender_11_out), .in1(shifter_2_out), .out(multiplexer_3_out), .sel(or_1_out));
  Shifter #(.shift("ar"), .width(32)) shifter_2 (.in(32'habcde000), .\dist (or_5_out), .out(shifter_2_out));
  // Probe on shifter_2_out
  Shifter #(.width(32)) shifter_3 (.in(A), .\dist (bit_extender_12_out), .out(sll1));
  assign slt2 = {{31{1'b0}}, comparator_4_lt};  // Bit_Extender bit_extender_16
  Shifter #(.shift("lr"), .width(32)) shifter_4 (.in(A), .\dist (bit_extender_13_out), .out(srl5));
  Shifter #(.shift("lr"), .width(64)) shifter_5 (.in(multiplier_2_out), .\dist (6'b100000), .out(shifter_5_out));
  Shifter #(.shift("lr"), .width(64)) shifter_6 (.in(multiplier_3_out), .\dist (6'b100000), .out(shifter_6_out));
  Shifter #(.shift("ar"), .width(32)) shifter_7 (.in(A), .\dist (bit_extender_14_out), .out(sra13));
  assign bit_extender_17_out = {{31{A[31]}}, A[31]};  // Bit_Extender bit_extender_17
  Shifter #(.shift("ar"), .width(32)) shifter_8 (.in(A), .\dist (or_7_out), .out(shifter_8_out));
  // Probe on multiplexer_2_out
  Bit_Extender #(.in_width(64), .out_width(32)) bit_extender_18 (.in(shifter_5_out), .out(mulh9));
  Bit_Extender #(.in_width(64), .out_width(32)) bit_extender_19 (.in(shifter_6_out), .out(mulhu11));
  Multiplexer #(.enable("false"), .width(32)) multiplexer_4 (
    .in0(bit_extender_17_out), .in1(shifter_8_out), .out(sra13), .sel(or_3_out));

  // Other names for the same wires on the sheet: bsel15[31:0] = B

  // Notes on the sheet:
  //   INPUTS to your circuit
  //   DON'T CHANGE THE LOCATIONS OF THE INPUTS AND OUTPUTS!
  //   OUTPUT from your circuit
endmodule
