// Logisim project cpu.circ as structural Verilog: 1 circuit, main circuit cpu
module cpu (
  input  clk,
  input  [31:0] Instruction,
  input  [31:0] MemReadData,
  output [31:0] MemAddress,
  output [31:0] ProgramCounter,
  output [31:0] ra,
  output [31:0] sp,
  output [31:0] t0,
  output [31:0] t1,
  output [31:0] t2,
  output [31:0] s0,
  output [31:0] s1,
  output [31:0] a0,
  output [3:0] MemWriteMask,
  output [31:0] MemWriteData
);

  wire and_1_out, and_2_out, and_3_out, and_4_out, and_5_out, and_6_out, ASel, BrEq, BrLt, BrUn, BSel,
       comparator_1_eq, comparator_2_eq, comparator_3_eq, comparator_4_eq, comparator_5_eq, comparator_6_eq,
       comparator_7_eq, comparator_8_eq, comparator_9_eq, comparator_10_eq, do_branch, imm7, imm20, imm31,
       MemWEn, not_1_out, not_2_out, not_3_out, or_1_out, or_2_out, or_3_out, or_4_out, or_5_out, or_6_out,
       PCSel, RegWEn;
  wire [1:0] funct7_edit, WBSel;
  wire [2:0] ImmSel;
  wire [3:0] ALUSel, format, imm11_8, undriven, undriven_2, undriven_3, undriven_4, undriven_5, undriven_6,
       undriven_7, undriven_8, undriven_9, undriven_10, undriven_11, undriven_12, undriven_13, undriven_14,
       undriven_15, undriven_16, undriven_17, undriven_18, undriven_19, undriven_20, undriven_21,
       undriven_22, undriven_23;
  wire [4:0] branch_store_dest, destReg, imm11_7, multiplexer_8_out, S_format_dest, undriven_24, undriven_25,
       undriven_26, undriven_27, undriven_28, undriven_29, undriven_30, undriven_31, undriven_32;
  wire [5:0] imm30_25;
  wire [6:0] imm31_25;
  wire [7:0] imm19_12;
  wire [9:0] imm30_21;
  wire [10:0] imm31_12;
  wire [11:0] imm31_20;
  wire [31:0] A, B, bit_extender_1_out, branch_store, DataToReg, I_imm_math, multiplexer_2_out, new_PC,
       no_branch, readReg1, RegWriteData;

  // Probe on do_branch
  Multiplexer #(.enable("false"), .width(32)) multiplexer_1 (
    .in0(no_branch), .in1(MemAddress), .out(new_PC), .sel(do_branch));
  Adder #(.width(32)) adder_1 (.a(ProgramCounter), .b(32'h4), .out(no_branch));  // open: cin, cout
  Register #(.width(32)) PC (.D(new_PC), .en(1'b1), .clk(clk), .Q(ProgramCounter));  // open: clr
  // Probe on Instruction[24:20]
  // Probe on Instruction[11:7]
  // Probe on Instruction[31:20]
  // Probe on Instruction[31:20]
  // Probe on Instruction[19:15]
  // Probe on RegWriteData
  // Probe on 32'hfffffffc
  // Probe on 32'hfffffffc
  // Probe on 32'hff842283
  // Probe on RegWEn
  // Probe on Instruction
  // Probe on ImmSel
  // Probe on Instruction[6:2]
  // Probe on Instruction[14:12]
  // Probe on Instruction[31:25]
  // Probe on funct7_edit
  // Probe on Instruction[19:15]
  // Probe on Instruction[24:20]
  // Probe on Instruction[11:7]
  // Probe on imm31
  // Probe on imm31_25
  // Probe on imm31_12
  // Probe on imm31_20
  // Probe on imm30_25
  // Probe on imm30_21
  // Probe on imm20
  // Probe on imm19_12
  // Probe on imm11_8
  // Probe on imm11_7
  // Probe on imm7
  // Probe on ImmSel
  // Probe on I_imm_math
  // Probe on RegWEn
  // Probe on PCSel
  control_logic control_logic_1 (
    .PCSel(PCSel), .RegWEn(RegWEn), .ImmSel(ImmSel), .BrUn(BrUn), .ASel(ASel), .BSel(BSel), .ALUSel(ALUSel),
    .MemWEn(MemWEn), .WBSel(WBSel), .Instruction(Instruction), .BrEq(BrEq), .BrLt(BrLt));
  Comparator #(.mode("unsigned"), .width(4)) comparator_1 (
    .a(format), .b(4'b0011), .eq(comparator_1_eq));  // open: gt, lt
  regfile regfile_1 (
    .ReadReg1(Instruction[19:15]), .ReadReg2(Instruction[24:20]), .WriteReg(Instruction[11:7]),
    .RegWriteData(RegWriteData), .RegWEn(RegWEn), .clk(clk), .ra(ra), .sp(sp), .t0(t0), .t1(t1), .t2(t2),
    .s0(s0), .s1(s1), .a0(a0), .RegReadData1(readReg1), .RegReadData2(branch_store));
  // Probe on branch_store
  imm_gen imm_gen_1 (.Instruction(Instruction), .ImmSel(ImmSel), .Immediate(I_imm_math));
  // Probe on ImmSel
  // Probe on comparator_1_eq
  Multiplexer #(.enable("false"), .width(32)) multiplexer_2 (
    .in0(readReg1), .in1(readReg1), .out(multiplexer_2_out), .sel(comparator_1_eq));
  assign bit_extender_1_out = {{27{1'b0}}, Instruction[19:15]};  // Bit_Extender bit_extender_1
  // Probe on readReg1
  // Probe on I_imm_math
  // Probe on I_imm_math
  // Probe on BrLt
  // Probe on BrEq
  // Probe on A
  // Probe on ASel
  // Probe on BrUn
  Multiplexer #(.enable("false"), .width(32)) multiplexer_3 (
    .in0(ProgramCounter), .in1(multiplexer_2_out), .out(A), .sel(ASel));
  // Probe on Instruction[6:2]
  // Probe on ASel
  // Probe on BSel
  // Probe on A
  // Probe on ALUSel
  // Probe on MemWEn
  // Probe on B
  // Probe on B
  // Probe on WBSel
  Multiplexer #(.enable("false"), .width(32)) multiplexer_4 (.in0(I_imm_math), .in1(branch_store), .out(B), .sel(BSel));
  // Probe on MemAddress
  alu alu_1 (.ALUResult(MemAddress), .A(A), .B(B), .ALUSel(ALUSel));
  // Probe on ALUSel
  branch_comp branch_comp_1 (.BrData1(readReg1), .BrData2(branch_store), .BrUn(BrUn), .BrEq(BrEq), .BrLt(BrLt));
  Multiplexer #(.enable("false"), .select(5), .width(4)) multiplexer_5 (
    .in0(4'b0000), .in1(undriven), .in2(undriven_2), .in3(undriven_3), .in4(4'b0001), .in5(4'b0010),
    .in6(undriven_4), .in7(undriven_5), .in8(4'b0011), .in9(undriven_6), .in10(undriven_7),
    .in11(undriven_8), .in12(4'b0100), .in13(4'b0101), .in14(undriven_9), .in15(undriven_10),
    .in16(undriven_11), .in17(undriven_12), .in18(undriven_13), .in19(undriven_14), .in20(undriven_15),
    .in21(undriven_16), .in22(undriven_17), .in23(undriven_18), .in24(4'b1000), .in25(4'b0111),
    .in26(undriven_19), .in27(4'b0110), .in28(undriven_20), .in29(undriven_21), .in30(undriven_22),
    .in31(undriven_23), .out(format), .sel(Instruction[6:2]));
  // Probe on MemAddress
  // Probe on format
  // Probe on MemAddress
  // Probe on MemAddress
  // Probe on MemWEn
  // Probe on RegWriteData
  Multiplexer #(.enable("false"), .select(2), .width(32)) multiplexer_6 (
    .in0(MemAddress), .in1(DataToReg), .in2(no_branch), .in3(I_imm_math), .out(RegWriteData), .sel(WBSel));
  // Probe on format
  // Probe on destReg
  Multiplexer #(.enable("false"), .select(4), .width(5)) multiplexer_7 (
    .in0(Instruction[11:7]), .in1(Instruction[11:7]), .in2(Instruction[11:7]), .in3(S_format_dest),
    .in4(Instruction[11:7]), .in5(Instruction[11:7]), .in6(Instruction[11:7]), .in7(Instruction[11:7]),
    .in8(branch_store_dest), .out(destReg), .sel(format));  // open: in9, in10, in11, in12, in13, in14, in15
  // Probe on multiplexer_8_out
  Multiplexer #(.enable("false"), .select(4), .width(5)) multiplexer_8 (
    .in0(undriven_24), .in1(undriven_25), .in2(undriven_26), .in3(undriven_27), .in4(undriven_28),
    .in5(undriven_29), .in6(undriven_30), .in7(undriven_31), .in8(undriven_32), .out(multiplexer_8_out),
    .sel(format));  // open: in9, in10, in11, in12, in13, in14, in15
  // Probe on MemWriteMask
  partial_store partial_store_1 (
    .Instruction(Instruction), .MemAddress(MemAddress), .DataFromReg(branch_store), .MemWEn(MemWEn),
    .MemWriteMask(MemWriteMask), .DataToMem(MemWriteData));
  // Probe on MemWriteData
  // Probe on DataToReg
  partial_load partial_load_1 (
    .Instruction(Instruction), .MemAddress(MemAddress), .DataFromMem(MemReadData), .DataToReg(DataToReg));
  Comparator #(.mode("unsigned"), .width(3)) comparator_2 (
    .a(Instruction[14:12]), .b(3'b100), .eq(comparator_2_eq));  // open: gt, lt
  Comparator #(.mode("unsigned"), .width(3)) comparator_3 (
    .a(Instruction[14:12]), .b(3'b110), .eq(comparator_3_eq));  // open: gt, lt
  Comparator #(.mode("unsigned"), .width(3)) comparator_4 (
    .a(Instruction[14:12]), .b(3'b000), .eq(comparator_4_eq));  // open: gt, lt
  not not_1 (not_1_out, BrEq);
  Comparator #(.mode("unsigned"), .width(3)) comparator_5 (
    .a(Instruction[14:12]), .b(3'b001), .eq(comparator_5_eq));  // open: gt, lt
  or or_1 (or_1_out, comparator_2_eq, comparator_3_eq);
  not not_2 (not_2_out, BrLt);
  Comparator #(.mode("unsigned"), .width(3)) comparator_6 (
    .a(Instruction[14:12]), .b(3'b101), .eq(comparator_6_eq));  // open: gt, lt
  Comparator #(.mode("unsigned"), .width(3)) comparator_7 (
    .a(Instruction[14:12]), .b(3'b111), .eq(comparator_7_eq));  // open: gt, lt
  and and_1 (and_1_out, BrEq, comparator_4_eq);
  and and_2 (and_2_out, not_1_out, comparator_5_eq);
  and and_3 (and_3_out, BrLt, or_1_out);
  or or_2 (or_2_out, comparator_6_eq, comparator_7_eq);
  or or_3 (or_3_out, and_1_out, and_2_out);
  and and_4 (and_4_out, not_2_out, or_2_out);
  or or_4 (or_4_out, or_3_out, and_3_out);
  Comparator #(.mode("unsigned"), .width(3)) comparator_8 (
    .a(ImmSel), .b(3'b010), .eq(comparator_8_eq));  // open: gt, lt
  or or_5 (or_5_out, or_4_out, and_4_out);
  // Probe on comparator_8_eq
  Comparator #(.mode("unsigned"), .width(4)) comparator_9 (
    .a(format), .b(4'b0110), .eq(comparator_9_eq));  // open: gt, lt
  Comparator #(.mode("unsigned"), .width(4)) comparator_10 (
    .a(format), .b(4'b0111), .eq(comparator_10_eq));  // open: gt, lt
  and and_5 (and_5_out, or_5_out, comparator_8_eq);
  not not_3 (not_3_out, PCSel);
  or or_6 (or_6_out, comparator_9_eq, comparator_10_eq);
  and and_6 (and_6_out, and_5_out, not_3_out);
  or or_7 (do_branch, and_6_out, or_6_out);

  // Other names for the same wires on the sheet: rs2[4:0] = Instruction[24:20]; funct7[6:0] = Instruction[31:25];
  //   ALU_result[31:0] = MemAddress; branched[31:0] = MemAddress; funct3[2:0] = Instruction[14:12];
  //   I_imm_math_dest[4:0] = Instruction[11:7]; I_load_dest[4:0] = Instruction[11:7];
  //   J_jal_dest[4:0] = Instruction[11:7]; J_jalr_dest[4:0] = Instruction[11:7];
  //   R_format_dest[4:0] = Instruction[11:7]; rd[4:0] = Instruction[11:7]; U_auipc_dest[4:0] = Instruction[11:7];
  //   U_lui_dest[4:0] = Instruction[11:7]; rs1[4:0] = Instruction[19:15]; opcode2_7[4:0] = Instruction[6:2];
  //   R_format[31:0] = branch_store; readReg2[31:0] = branch_store; S_format[31:0] = branch_store

  // Notes on the sheet:
  //   PCSel Key:
  //   0 for PC + 4
  //   To IMEM
  //   1 for branch / jump PC imm
  //   IMEM (do **NOT** move this)
  //   change no-branch to ProgramCounter to undo
  //   change PC or ProgramCounter?
  //   From IMEM
  //   opcode
  //   funct3 (might have a problem being undefined)
  //   Note: funct_comb not yet defined
  //   0b0 --> 0x0
  //   only need to deal with only first and last bit
  //   0b10 = 2 --> 0x20
  //   0b01 = 1 --> 0x01
  //   Key:
  //   I-Format --> Load = 0
  //   U-Format auipc = 2
  //   S-Format = 3
  //   R-Format = 4
  //   U-Format lui = 5
  //   I-Formal jal = 6
  //   J-Format jalr = 7
  //   Branch / Store = 8
  //   use format to determine processing funct7 in conjunction with funct3
  //   can do addition for selection of item; use opcode as input; and output being funct_comb
  //   funct7 = 0, 0x20 (100000), or 0x01 (01) 
  //   0 = imm
  //   1 = register
  //   jal --> A = 0, B = 0
  //   jalr --> A = 1, B = 0
  //   I-Format --> imm log/arith = 1
  //   Inputs/Outputs for testing. Do **NOT** move these.
  //   It is OK to move the PC, RegFile, ALU, MEM, Branch Comp, Imm Gen, Partial Load, Partial Store and Control Logic to wherever is most convenient for you when constructing your CPU, and to delete this text
  //   either a register read value or an immediate
  //   These These determine what format to use in with less overall values
  //   still need to put RD for S, Branch
  //   Opcodes:
  //   R-Format: 12
  //   S-Format = 8
  //   Branch / Store = 24
  //   J-Format --> jal: 27; jalr: 25
  //   U-Format --> lui = 13; auipc = 5
  //   This row has St_B_MemWEn; comparisons for Branch (BrData1, BrData2, BrUn, BrEq, BrLt)
  //   This row has BrUn, ASel, BSel, I_format_alu, I_funct7
  //   I-Type --> immediate log/arith = 4; load = 0
  //   This row has template, MemWEn, RegWEn, WBSel, funct7_edit
  //   and R_format_alu, R_funct7
  //   These determine what the return register is
  //   still need to put RD for S, Branch
  //   To DMEM
  //   [Template]
  //   ALU Key:
  //   add = 0
  //   sll = 1
  //   slt = 2
  //   srl = 5
  //   xor = 4
  //   or = 6
  //   and = 7
  //   sub = 12
  //   sra = 13
  //   S-Format = 3
  //   R-Format = 4
  //   mul (sign) = 8
  //   mulh (sign) = 9
  //   mulhu = 11
  //   bsel = 15
  //   DMEM (do **NOT** move this)
  //   Key:
  //   I-Fomat --> Load = 0
  //   I-Format --> imm log/arith = 1
  //   U-Format auipc = 2
  //   U-Format lui = 5
  //   J-Formal jal = 6
  //   J-Format jalr = 7
  //   Branch / Store = 8
  //   Key:
  //   I-Fomat --> Load = 0
  //   I-Format --> imm log/arith = 1
  //   U-Format auipc = 2
  //   S-Format = 3
  //   R-Format = 4
  //   U-Format lui = 5
  //   J-Formal jal = 6
  //   J-Format jalr = 7
  //   Branch / Store = 8
  //   From DMEM
  //   Branch Funct3 Key:
  //   0 = beq
  //   1 = bne
  //   4 = blt
  //   5 = bge
  //   6 = bltu (unsigned)
  //   7 = bgeu (unsigned)
  //   (same circuit for bltu, blt; bge, bgeu)
  //   jumps
  //   branches
endmodule
