// Logisim project imm-gen.circ as structural Verilog: 1 circuit, main circuit imm_gen
module imm_gen (
  input  [31:0] Instruction,
  input  [2:0] ImmSel,
  output [31:0] Immediate
);

  wire [31:0] Branch_imm, I_imm, J_imm, S_imm;

  assign I_imm = {{20{Instruction[31]}}, Instruction[31:20]};  // Bit_Extender bit_extender_1
  assign S_imm = {{20{Instruction[31]}}, {Instruction[31:25], Instruction[11:7]}};  // Bit_Extender bit_extender_2
  assign Branch_imm = {{19{Instruction[31]}}, {Instruction[31], Instruction[7], Instruction[30:25], Instruction[11:8], 1'b0}};  // Bit_Extender bit_extender_3
  assign J_imm = {{11{Instruction[31]}}, {Instruction[31], Instruction[19:12], Instruction[20], Instruction[30:21], 1'b0}};  // Bit_Extender bit_extender_4
  Comparator #(.width(3)) comparator_1 (.a(Instruction[14:12]));  // open: b, gt, eq, lt
  Multiplexer #(.enable("false"), .select(3), .width(32)) multiplexer_1 (
    .in0(I_imm), .in1(S_imm), .in2(Branch_imm), .in3({Instruction[31:12], {12{1'b0}}}), .in4(J_imm),
    .out(Immediate), .sel(ImmSel));  // open: in5, in6, in7

  // Other names for the same wires on the sheet: funct3[2:0] = Instruction[14:12]; imm19_12[7:0] = Instruction[19:12];
  //   imm31_12[19:0] = Instruction[31:12]; U_imm[31:12] = Instruction[31:12]; imm4_0[4:0] = Instruction[11:7];
  //   imm11_b = Instruction[7]; imm4_1[3:0] = Instruction[11:8]; imm10_1[9:0] = Instruction[30:21];
  //   imm10_5[5:0] = Instruction[30:25]; imm11_0[11:0] = Instruction[31:20]; imm11_5[6:0] = Instruction[31:25];
  //   imm12_b = Instruction[31]; imm20_j = Instruction[31]; imm11_j = Instruction[20]

  // Notes on the sheet:
  //   INPUTS to your circuit
  //   want 31-20
  //   Load instructions a little complicated (I-format)
  //   I don't know what to bit for bit 0; leaving it as 0
  //   note that this is 0-extended because I'm not quite sure what to do here :)
  //   This circuit generates immediates
  //   b6-7
  //   20-25
  //   b31-20
  //   26-31
  //   imm[11:0], 31-20
  //   note that this is 0-extended because I'm not quite sure what to do here :)
  //   ImmSel Key:
  //   I-Format = 0
  //   U-Format = 1
  //   S-Format = 2
  //   R-Format = 3
  //   J-Format = 4
  //   Branch-Format = 5
  //   b7
  //   imm11_0 indicates what position in array
  //   25
  //   I-Format
  //   S-Format
  //   Branch-Format
  //   J-Format
  //   U-Format
  //   DON'T CHANGE THE LOCATIONS OF THE INPUTS AND OUTPUTS!
  //   undefined
  //   need to still account for shift immediate (I-Format) actions w/ opcode & funct3
  //   OUTPUT from your circuit
endmodule
